# Fritzing sketch pwm (saved by Fritzing 0.7.12b)
breadboards: 1

parts:
  U1 = 555 Timer [package="DIP8 [THT]"]
  C3 = Electrolytic Capacitor [capacitance=10nF package="100 mil [THT, electrolytic]"]
  D2 = Rectifier Diode [part_number=1n4148 breakdown_voltage=3.6V package="300 mil [THT]"]
  R2 = Resistor [tolerance=±5% resistance=100 package=THT]
  R4 = Resistor [tolerance=±5% resistance=100 package=THT]
  R5 = Resistor [tolerance=±5% resistance=100 package=THT]
  C5 = Electrolytic Capacitor [package="100 mil [THT, electrolytic]"]
  C2 = Electrolytic Capacitor [capacitance=1µF package="100 mil [THT, electrolytic]"]
  C4 = Electrolytic Capacitor [capacitance=47µF package="100 mil [THT, electrolytic]"]
  C1 = Ceramic Capacitor [capacitance=10nF package="200 mil [THT, multilayer]"]
  D3 = Rectifier Diode [part_number=1n4148 package="300 mil [THT]"]
  U2 = 555 Timer [package="DIP8 [THT]"]
  C6 = Ceramic Capacitor [capacitance=10nF package="200 mil [THT, multilayer]"]
  D4 = Rectifier Diode [part_number=1n4148 package="300 mil [THT]"]
  D5 = Rectifier Diode [part_number=1n4148 breakdown_voltage=3.6V package="300 mil [THT]"]
  R8 = Resistor [tolerance=±5% resistance=100 package=THT]
  R9 = Resistor [tolerance=±5% resistance=100 package=THT]
  R10 = Resistor [tolerance=±5% resistance=100 package=THT]
  C10 = Electrolytic Capacitor [package="100 mil [THT, electrolytic]"]
  C11 = Ceramic Capacitor [capacitance=0.22mF voltage=20V package="100 mil [THT, multilayer]"]
  C12 = Ceramic Capacitor [capacitance=0.1mF voltage=20V package="100 mil [THT, multilayer]"]
  C13 = Ceramic Capacitor [capacitance=10nF voltage=20V package="100 mil [THT, multilayer]"]
  R12 = Resistor [tolerance=±20% resistance=220 package=THT]
  R13 = Resistor [tolerance=±5% resistance=1k package=THT]
  Q1 = Basic FET N-Channel [package="TO220 [THT]"]
  D6 = Rectifier Diode [part_number=1N4001 package="300 mil [THT]"]
  S1 = Toggle Switch [package=THT]
  VCC1 = Battery
  S2 = Toggle Switch [package=THT]
  R14 = Rotary Potentiometer (Small) [maximum_resistance=10kΩ]
  R15 = Rotary Potentiometer (Small) [maximum_resistance=50kΩ]
  R16 = Rotary Potentiometer (Small) [maximum_resistance=10kΩ]
  R17 = Rotary Potentiometer (Small) [maximum_resistance=50kΩ]
  J1 = Screw terminal - 2 pins [package=THT]
  J2 = female pin header, 3 pins [form="♀ (female)"]  # not connected

nets:
  N1: U1.Ground, C5.-, C1.0, U2.Ground, C6.0, C10.-, R13.Pin_1, Q1.source, S1.COM, VCC1.-, S2.COM
  N2: U1.Trigger, U1.Threshold, C3.+, D2.anode, C2.+, C4.+, D3.cathode
  N3: U1.Output, U2.Reset
  N4: U1.Reset, U1.Vcc_Supply_Voltage, R4.Pin_0, R5.Pin_1, C5.+
  N5: U1.Control_Voltage, C1.1
  N6: U1.Discharge, R2.Pin_0, D3.anode, R14.leg1
  N7: C3.-, S2.L1
  N8: D2.cathode, R15.leg2
  N9: R2.Pin_1, R15.wiper
  N10: R4.Pin_1, R14.wiper
  N11: R5.Pin_0, R8.Pin_0, D6.cathode, VCC1.+, J1.pin1
  N12: C2.-, S2.L2
  N13: C4.-, C13.0
  N14: U2.Trigger, U2.Threshold, D4.cathode, D5.anode, C11.1, C12.1, C13.1
  N15: U2.Output, R12.Pin_0
  N16: U2.Control_Voltage, C6.1
  N17: U2.Discharge, D4.anode, R10.Pin_0, R16.leg1
  N18: U2.Vcc_Supply_Voltage, R8.Pin_1, R9.Pin_0, C10.+
  N19: D5.cathode, R17.leg2
  N20: R9.Pin_1, R16.wiper
  N21: R10.Pin_1, R17.wiper
  N22: C11.0, S1.L2
  N23: C12.0, S1.L1
  N24: R12.Pin_1, R13.Pin_0, Q1.gate
  N25: Q1.drain, D6.anode, J1.pin2

custom parts:
  Electrolytic Capacitor: A small electrolytic capacitor
